# Fritzing sketch CCD-Array-Spectrometer-Fritzing (saved by Fritzing 0.9.1b)
breadboards: 1

parts:
  LED1 = LED - 5mm [color="White (4500K)" package="5 mm [THT]"]
  U1 = mystery part, 13 pins [chip_label=TSL1406R part_number=TSL1406R]
  Onderdeel1 = Arduino Uno (Rev3)
  R1 = Resistor [tolerance=±5% resistance=220 package=THT]
  C1 = Electrolytic Capacitor [capacitance=0.1mF package="100 mil [THT, electrolytic]"]

nets:
  N1: LED1.cathode, U1.pin1, U1.pin5, Onderdeel1.GND, C1.-
  N2: LED1.anode, R1.Pin_1
  N3: U1.pin2, U1.pin3, U1.pin9, Onderdeel1.D2
  N4: U1.pin4, U1.pin10, Onderdeel1.D3_PWM
  N5: U1.pin6, U1.pin12, Onderdeel1.A0
  N6: U1.pin7, U1.pin8
  N7: U1.pin13, Onderdeel1.5V, C1.+
  N8: Onderdeel1.A5/SCL, R1.Pin_0
