# Fritzing sketch CCD-Array-Spectrometer-Fritzing (saved by Fritzing 0.9.3b)
breadboards: 1

parts:
  LED1 = LED - 5mm [color="White (4500K)" package="5 mm [THT]"]
  U1 = mystery part, 13 pins [chip_label=TSL1406R part_number=TSL1406R]
  Onderdeel1 = Arduino Uno (Rev3)
  R1 = Resistor [tolerance=±5% resistance=220 package=THT]
  C1 = Electrolytic Capacitor [capacitance=0.1mF package="100 mil [THT, electrolytic]"]
  LED2 = RGB LED (com. cathode, rgb) [package="5 mm [THT]"]
  R2 = Resistor [tolerance=±5% resistance=220 package=THT]
  R3 = Resistor [tolerance=±5% resistance=220 package=THT]
  R4 = Resistor [tolerance=±5% resistance=220 package=THT]
  C2 = Electrolytic Capacitor [capacitance=0.1mF package="100 mil [THT, electrolytic]"]

nets:
  N1: LED1.cathode, U1.pin1, U1.pin5, Onderdeel1.GND, C1.-, LED2.common_cathode, C2.-
  N2: LED1.anode, R1.Pin_1
  N3: U1.pin2, U1.pin3, U1.pin9, Onderdeel1.D2
  N4: U1.pin4, U1.pin10, Onderdeel1.D3_PWM
  N5: U1.pin6, U1.pin12, Onderdeel1.A0
  N6: U1.pin7, U1.pin8
  N7: U1.pin13, Onderdeel1.5V, C1.+, C2.+
  N8: Onderdeel1.A5/SCL, R1.Pin_0
  N9: Onderdeel1.D8, R2.Pin_0
  N10: Onderdeel1.D9_PWM, R3.Pin_1
  N11: Onderdeel1.D10_PWM/SS, R4.Pin_1
  N12: LED2.red_anode, R2.Pin_1
  N13: LED2.green_anode, R4.Pin_0
  N14: LED2.blue_anode, R3.Pin_0
